# Fritzing sketch traethlin (saved by Fritzing 0.9.6b)

parts:
  Mod1 = Raspberry Pi 4B
  A1 = ESP32 Wroom 32E dev board
  Steering = Basic Servo
  Front_diff = Basic Servo
  Rear_diff = Basic Servo
  ESC = Dagu DGServo 9g header connector (female) [package=THT]
  DC1 = DC_DC_XL4016 [package=board_screw]
  Gearbox = Basic Servo
  5V = Screw terminal - 2 pins [package=THT]
  3_3V = Screw terminal - 2 pins [package=THT]
  GND = Screw terminal - 2 pins [package=THT]
  U1 = WS2812 RGB LED strip

nets:
  N1: Mod1.3V3, A1.Pin_1, 3_3V.pin1, 3_3V.pin2
  5V: Mod1.5V, DC1.OUT+, 5V.pin1, 5V.pin2, U1.VCC
  GND: Mod1.GND, A1.Pin_38, DC1.OUT-, GND.pin1, GND.pin2, U1.GND
  N2: A1.Pin_27, Steering.pulse
  N3: A1.Pin_28, ESC.pulse
  N4: A1.Pin_29, Front_diff.pulse
  N5: A1.Pin_30, Rear_diff.pulse
  N6: A1.Pin_31, Gearbox.pulse
  N7: A1.Pin_37, U1.DIN
  VCC: Steering.vcc, Front_diff.vcc, Rear_diff.vcc, ESC.Vcc, DC1.IN+, Gearbox.vcc
  GND_2: Rear_diff.gnd, ESC.gnd, DC1.IN-, Gearbox.gnd

custom parts:
  ESP32 Wroom 32E dev board: The ESP32 WROOM-32E is a versatile and powerful module built around Espressif’s ESP32 chipset. It offers dual-core processing, integrated Wi-Fi and Bluetooth connectivity, and boasts a wide range of peripheral interfaces.
  WS2812 RGB LED strip: WS2812 strip
